# Fritzing sketch Esquematico 1 motor (saved by Fritzing 0.9.0b)

parts:
  Componente1 = Arduino Mega ADK (Rev3)
  U1 = L298 [package=multiwatt15_6400bgheatsink]
  R1 = Rotary Potentiometer (Large) [maximum_resistance=5kΩ package=THT]
  D2 = Rectifier Diode [package="Melf DO-213 AA [SMD]"]
  D3 = Rectifier Diode [package="Melf DO-213 AA [SMD]"]
  D4 = Rectifier Diode [package="Melf DO-213 AA [SMD]"]
  D5 = Rectifier Diode [package="Melf DO-213 AA [SMD]"]
  M1 = DC Motor
  C2 = Capacitor [package=cap-pth-small]
  V1 = DC Power [voltage=7V]
  V2 = DC Power [voltage=5V]
  V3 = DC Power [voltage=7V]
  V4 = DC Power [voltage=5V]

nets:
  N1: Componente1.A1, R1.wiper
  GND: Componente1.GND, U1.GND, R1.leg1, D3.anode, D5.anode, C2.2, V1.V-, V2.V-, V3.V-, V4.V-
  N2: Componente1.D6_PWM, U1.IN1
  N3: Componente1.D7_PWM, U1.IN2
  N4: Componente1.D33, U1.ENA
  N5: U1.OUT1, D2.anode, D5.cathode, M1.pin_1
  N6: U1.OUT2, D3.cathode, D4.anode, M1.pin_2
  N7: U1.VS, V3.V+
  N8: U1.VLS, V4.V+
  N9: R1.leg2, V2.V+
  N10: D2.cathode, D4.cathode, C2.1, V1.V+
